# Fritzing sketch Project2 (saved by Fritzing 0.9.3b)
breadboards: 1

parts:
  Part1 = Arduino Nano 33 IOT
  JP1 = Header 3 [package=1x03-1mm-ra]
  JP2 = Header 3 [package=1x03-1mm-ra]

nets:
  N1: Part1.RESET, Part1.A7
  N2: Part1.GND, Part1.D13~, JP1.2
  N3: Part1.D11/MOSI, Part1.+5V
  N4: Part1.A1, JP2.1
  N5: Part1.A0, JP1.1
  N6: Part1.3V3, JP2.2

notes:
  Sound Sensor
  Piezo Sensor

custom parts:
  Arduino Nano 33 IOT: The Arduino Nano 33 IoT is the easiest and cheapest point of entry to enhance existing devices (and creating new ones) to be part of the IoT and designing pico-network applications. Whether you are looking at building a sensor network connected to your office or home router, or if you want to create a BLE device sending data to a cellphone, the Nano 33 IoT is your one-stop-solution for many of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
