# Fritzing sketch Project1 (saved by Fritzing 0.9.3b)
breadboards: 1

parts:
  Part1 = Arduino Nano 33 IOT
  R1 = Resistor [tolerance=±5% resistance=220 package=THT]
  R2 = Resistor [tolerance=±5% resistance=220 package=THT]
  R3 = Resistor [tolerance=±5% resistance=220 package=THT]
  R4 = Resistor [tolerance=±5% resistance=220 package=THT]
  LED1 = LED - 5mm [color="Red (635nm)" package="5 mm [THT]"]
  LED2 = LED - 5mm [color="Yellow (585nm)" package="5 mm [THT]"]
  LED3 = LED - 5mm [color="White (6500K)" package="5 mm [THT]"]
  LED4 = LED - 5mm [color="Green (555nm)" package="5 mm [THT]"]
  JP1 = Header 3 [package=1x03-1mm-ra]
  JP2 = Header 3 [package=1x03-1mm-ra]
  JP3 = Header 3 [package=1x03-1mm-ra]

nets:
  N1: Part1.RESET, Part1.A7
  N2: Part1.GND, Part1.D13~, R1.Pin_1, R2.Pin_1, R3.Pin_1, JP2.2, JP3.2
  N3: Part1.D3~, JP2.1
  N4: Part1.D4, JP3.1
  N5: Part1.D5~, LED2.cathode
  N6: Part1.D7, LED1.cathode
  N7: Part1.D8, LED4.cathode
  N8: Part1.D9~, LED3.cathode
  N9: Part1.D11/MOSI, Part1.+5V
  N10: Part1.3V3, R4.Pin_1, JP1.3
  N11: R1.Pin_0, LED2.anode
  N12: R2.Pin_0, LED3.anode
  N13: R3.Pin_0, LED1.anode
  N14: R4.Pin_0, LED4.anode

custom parts:
  Arduino Nano 33 IOT: The Arduino Nano 33 IoT is the easiest and cheapest point of entry to enhance existing devices (and creating new ones) to be part of the IoT and designing pico-network applications. Whether you are looking at building a sensor network connected to your office or home router, or if you want to create a BLE device sending data to a cellphone, the Nano 33 IoT is your one-stop-solution for many of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
